# Fritzing sketch Proje (saved by Fritzing 0.9.3b)

parts:
  Parça1 = FC-28 Soil Hygrometer Module - Probe
  Parça2 = FC-28 Soil Hygrometer Module
  U1 = ESP8266 NodeMCU LoLin module

nets:
  N1: Parça1.POS, Parça2.POS
  N2: Parça1.NEG, Parça2.NEG
  VCC: Parça2.VCC, U1.3V3
  GND: Parça2.GND, U1.GND
  N3: Parça2.AO, U1.A0

notes:
  Kullanılan Malzemeler :
  1 - NodeMCU ESP8266
  2 - Toprak Nem Sensörü
  3 - 5 adet Jumper Kablo
  Hazırlayan
  Ad Soyad : İsa Emre Konuk
  No : G221210306

custom parts:
  FC-28 Soil Hygrometer Module - Probe: The FC-28 is a soil hygrometer module that uses the Texas Instruments LM393 comparator chip to provide an analog measurement of soil humidity.
  FC-28 Soil Hygrometer Module: The FC-28 is a soil hygrometer module that uses the Texas Instruments LM393 comparator chip to provide an analog measurement of soil humidity. The digital output is high when soil moisture is over a certain threshold, as determined by adjusting the potentiometer.
  ESP8266 NodeMCU LoLin module: ESP8266 based NodeMCU
